// Logisim project ProjectCOA_demo.circ as structural Verilog: 6 circuits, main circuit ALU
module main (
);

  wire clock_1_out, control_unit_1_alu_op, control_unit_1_ld_a, control_unit_1_ld_b, control_unit_1_sel,
       undriven_2;
  wire [7:0] adder_1_out, multiplexer_1_out, PC_q, ram_1_data, Reg_A_q, Reg_B_q, rom_1_data, undriven;

  ROM rom_1 (.addr(PC_q), .data(rom_1_data));  // open: sel
  Clock clock_1 (.out(clock_1_out));
  Register_part PC (.D(adder_1_out), .Q(PC_q), .clk(clock_1_out));  // open: en, clr
  Control_Unit control_unit_1 (
    .Op1(rom_1_data[6]), .Op0(rom_1_data[7]), .Ld_A(control_unit_1_ld_a), .Ld_B(control_unit_1_ld_b),
    .Sel(control_unit_1_sel), .ALU_Op(control_unit_1_alu_op));
  Adder adder_1 (.a(PC_q), .b(8'h1), .out(adder_1_out));  // open: cin, cout
  Register_part Reg_A (.D(undriven), .en(control_unit_1_ld_a), .Q(Reg_A_q), .clk(clock_1_out));  // open: clr
  Register_part Reg_B (.D(undriven), .en(control_unit_1_ld_b), .Q(Reg_B_q), .clk(clock_1_out));  // open: clr
  Multiplexer #(.width(8)) multiplexer_1 (
    .in0(ram_1_data), .in1(undriven), .out(multiplexer_1_out), .sel(control_unit_1_sel));  // open: en
  ALU alu_1 (
    .Reg_A(Reg_A_q), .Reg_B(Reg_B_q), .OE(control_unit_1_alu_op), .ALU_Result(multiplexer_1_out));  // open: ALU_Op, Dout, Carry_out, in_5
  RAM #(.addrWidth(6)) ram_1 (
    .addr(rom_1_data[5:0]), .data(ram_1_data), .sel(1'b1), .clk(undriven_2), .ld(1'b1), .clr(1'b0));

  // Notes on the sheet:
  //   contents of rom_1 (hex, n*v repeats v):
  //   0 5 14*0 1 43 14*0 2 80
endmodule

module ALU (
  input  [7:0] Reg_A,
  input  [7:0] Reg_B,
  input  OE,
  input  ALU_Op,
  input  in_5,
  output [7:0] Dout,
  output [7:0] ALU_Result,
  output Carry_out
);

  wire adder_1_cout;
  wire [7:0] adder_1_out, subtractor_1_out;

  Adder adder_1 (.a(Reg_A), .b(Reg_B), .out(adder_1_out), .cout(adder_1_cout));  // open: cin
  Subtractor subtractor_1 (.a(Reg_A), .b(Reg_B), .out(subtractor_1_out), .bin(adder_1_cout), .bout(Carry_out));
  Multiplexer #(.width(8)) multiplexer_1 (
    .in0(adder_1_out), .in1(subtractor_1_out), .out(ALU_Result), .sel(ALU_Op), .en(in_5));
  assign Dout = OE ? ALU_Result : 8'bz;  // Controlled_Buffer controlled_buffer_1

  // Notes on the sheet:
  //   ALU(8 bits）
endmodule

module Memory_cell (
  input  clock,
  input  WE,
  input  Din,
  input  OE,
  input  Reset,
  output Dout,
  output Stored_Data
);

  wire and_1_out, and_2_out, not_1_out, or_1_out;

  not not_1 (not_1_out, WE);
  and and_1 (and_1_out, Stored_Data, not_1_out);
  and and_2 (and_2_out, WE, Din);
  or or_1 (or_1_out, and_1_out, and_2_out);
  D_Flip_Flop d_ff_1 (.clk(clock), .D(or_1_out), .Q(Stored_Data), .reset(Reset));  // open: Qn, preset, en
  assign Dout = OE ? Stored_Data : 1'bz;  // Controlled_Buffer controlled_buffer_1

  // Notes on the sheet:
  //   Memory Cell
endmodule

module Register (
  input  clock,
  input  WE,
  input  [7:0] Din,
  input  OE,
  output [7:0] Dout,
  output [7:0] Stored_Data
);

  Memory_cell _0 (
    .clock(clock), .WE(WE), .Din(Din[0]), .OE(OE), .Dout(Dout[0]), .Stored_Data(Stored_Data[0]));  // open: Reset
  Memory_cell _1 (
    .clock(clock), .WE(WE), .Din(Din[1]), .OE(OE), .Dout(Dout[1]), .Stored_Data(Stored_Data[1]));  // open: Reset
  Memory_cell _2 (
    .clock(clock), .WE(WE), .Din(Din[2]), .OE(OE), .Dout(Dout[2]), .Stored_Data(Stored_Data[2]));  // open: Reset
  Memory_cell _3 (
    .clock(clock), .WE(WE), .Din(Din[3]), .OE(OE), .Dout(Dout[3]), .Stored_Data(Stored_Data[3]));  // open: Reset
  Memory_cell _4 (
    .clock(clock), .WE(WE), .Din(Din[4]), .OE(OE), .Dout(Dout[4]), .Stored_Data(Stored_Data[4]));  // open: Reset
  Memory_cell _5 (
    .clock(clock), .WE(WE), .Din(Din[5]), .OE(OE), .Dout(Dout[5]), .Stored_Data(Stored_Data[5]));  // open: Reset
  Memory_cell _6 (
    .clock(clock), .WE(WE), .Din(Din[6]), .OE(OE), .Dout(Dout[6]), .Stored_Data(Stored_Data[6]));  // open: Reset
  Memory_cell _7 (
    .clock(clock), .WE(WE), .Din(Din[7]), .OE(OE), .Dout(Dout[7]), .Stored_Data(Stored_Data[7]));  // open: Reset

  // Notes on the sheet:
  //   Register (8bit)
endmodule

module Decoder (
  input  in_1,
  input  [2:0] in_2,
  output out_3,
  output out_4,
  output out_5,
  output out_6,
  output out_7,
  output out_8,
  output out_9,
  output out_10
);

  Decoder_part #(.select(3)) decoder_1 (
    .out0(out_3), .out1(out_4), .out2(out_5), .out3(out_6), .out4(out_7), .out5(out_8), .out6(out_9),
    .out7(out_10), .sel(in_2), .en(in_1));

  // Notes on the sheet:
  //   3 to 8 Decoder
endmodule

module Control_Unit (
  input  Op1,
  input  Op0,
  output Ld_A,
  output Ld_B,
  output Sel,
  output ALU_Op
);

  wire not_1_out, not_2_out;

  not not_1 (not_1_out, Op0);
  not not_2 (not_2_out, Op1);
  or or_1 (Ld_A, not_1_out, Op1);
  and and_1 (Ld_B, not_2_out, Op0);

  assign ALU_Op = Op0;
  assign Sel = Op1;
endmodule
